# Fritzing sketch bluetoothBuddy (saved by Fritzing 0.9.3b)
breadboards: 1

parts:
  Part1 = Arduino Nano (Rev3.0)
  Part2 = Bluetooth HC-05 Macho
  R1 = Resistor [tolerance=±5% resistance=220 package=THT]
  LED1 = LED - 5mm [color="Red (633nm)" package="5 mm [THT]"]
  SP1 = SPEAKER [package=pcb_mount_speaker]
  S1 = Momentary Switch [package=ksa_sealed_tac_switch]
  R2 = Resistor [tolerance=±5% resistance=220 package="0603 [SMD]"]

nets:
  N1: Part1.D1/TX, Part2.RXD
  N2: Part1.D0/RX, Part2.TXD
  GND: Part1.GND, Part2.GND, R1.Pin_0, SP1.+, S1.2, R2.Pin_0
  N3: Part1.D2, LED1.cathode
  N4: Part1.D3, S1.3
  5V: Part1.5V, Part2.VCC, S1.4
  N5: Part1.A1, SP1.-
  N6: R1.Pin_1, LED1.anode
  N7: S1.1, R2.Pin_1
